# Fritzing sketch Sem6_PCBv2 (saved by Fritzing 0.9.3b)
circuit board: 5.86596cm x 4.41662cm
breadboards: 1

parts:
  DroneDOF_Custom_PCB = Raspberry Pi 3 [part_number=RPI-3-V1.2]
  JP1 = Header 12 [package=1x12_machine-pin-header_lock.004]
  JP2 = Header 12 [package=1x12_machine-pin-header_lock.004]

nets:
  3V3: DroneDOF_Custom_PCB.3v3, DroneDOF_Custom_PCB.3V3, JP1.8, JP2.3, JP2.12
  N1: DroneDOF_Custom_PCB.GPIO2, JP1.2, JP1.12, JP2.9
  N2: DroneDOF_Custom_PCB.GPIO3, JP1.3, JP1.11, JP2.1, JP2.10
  N3: DroneDOF_Custom_PCB.GND, JP1.1, JP1.7, JP2.4, JP2.7, JP2.11
